// Logisim project sCPU_F6_sub.circ as structural Verilog: 8 circuits, main circuit main
module main (
);

  clock_reset clock_reset_1 ();  // open: clk_in, rst_in, ck_r0, rst_r0, ck_pc, rst_pc, ck_r1, rst_r1, rst_r2, ck_r2, ck_r3, rst_r3, ck_out, rst_out
  pc pc_1 ();  // open: ck, clr, rst_and, mux_sel, branch_offset, pc_q_fetch, pc_q
  fetch_decode fetch_decode_1 ();  // open: pc_addr, opcode_hi, opcode_lo, rs1_fan0, rs1_addr, rs1_fan1, rs2_imm, rs2_fan0, rs2_fan1, dec_out0, dec_out1, dec_out2, dec_out3
  gpr_rmux gpr_rmux_1 ();  // open: en_r0, d_r0, ck_r0, clr_r0, rmux1_sel_ab, rmux1_sel_top, en_r1, d_r1, ck_r1, clr_r1, rmux1_sel_cd, en_r2, rmux2_sel_ab, d_r2, ck_r2, clr_r2, rmux2_sel_top, rmux2_sel_cd, en_r3, d_r3, ck_r3, clr_r3, raddr_out, rmux1_out, rmux2_out
  control control_1 ();  // open: comp_eq, dec3, dec0, dec1, waddr, wen0, branch_taken, wen1, is_gpr_write, wen2, wen3
  alu alu_1 ();  // open: a, b, sum, eq
  writeback writeback_1 ();  // open: alu_result, is_li, is_io, imm_in, out_d, ck, clr, wdata, imm_out_to_mux
endmodule

module clock_reset (
  input  clk_in,
  input  rst_in,
  output ck_r0,
  output rst_r0,
  output ck_pc,
  output rst_pc,
  output ck_r1,
  output rst_r1,
  output rst_r2,
  output ck_r2,
  output ck_r3,
  output rst_r3,
  output ck_out,
  output rst_out
);


  assign ck_out = clk_in;
  assign ck_pc = clk_in;
  assign ck_r3 = clk_in;
  assign rst_out = rst_in;
  assign rst_r1 = rst_r0;
  assign rst_r2 = rst_r0;
  assign rst_r3 = rst_r0;
endmodule

module pc (
  input  ck,
  input  clr,
  input  rst_and,
  input  mux_sel,
  input  [1:0] branch_offset,
  output [7:0] pc_q_fetch,
  output [7:0] pc_q
);

  wire and_1_out;
  wire [7:0] adder_1_out, bit_extender_1_out;

  Register #(.width(8)) PC (.D(adder_1_out), .en(and_1_out), .Q(pc_q), .clk(ck), .clr(clr));
  Adder #(.width(8)) adder_1 (.a(pc_q), .b(8'h1), .out(adder_1_out), .cin(1'b0));  // open: cout
  assign bit_extender_1_out = {{6{branch_offset[1]}}, branch_offset};  // Bit_Extender bit_extender_1
  Multiplexer #(.width(8)) multiplexer_1 (
    .in0(8'h1), .in1(bit_extender_1_out), .out(adder_1_out), .sel(mux_sel));  // open: en
  and and_1 (and_1_out, rst_and, 1'b1);

  assign pc_q_fetch = pc_q;
endmodule

module fetch_decode (
  input  [7:0] pc_addr,
  output [1:0] opcode_hi,
  output [1:0] opcode_lo,
  output rs1_fan0,
  output [1:0] rs1_addr,
  output rs1_fan1,
  output [1:0] rs2_imm,
  output rs2_fan0,
  output rs2_fan1,
  output dec_out0,
  output dec_out1,
  output dec_out2,
  output dec_out3
);

  ROM #(.addrWidth(8), .dataWidth(8)) rom_1 (.data({opcode_hi, opcode_lo, rs1_addr, rs2_fan1, rs2_fan0}));  // open: addr
  Decoder #(.select(2), .enable("false")) decoder_1 (
    .out0(dec_out0), .out1(dec_out1), .out2(dec_out2), .out3(dec_out3), .sel(opcode_hi));

  assign rs1_fan0 = rs1_addr[0];
  assign rs1_fan1 = rs1_addr[1];
  assign rs2_imm = {rs2_fan1, rs2_fan0};

  // Notes on the sheet:
  //   contents of rom_1 (hex, n*v repeats v):
  //   0 90 1 a1 2 be 3 16 4 29 5 f7 6 54 7 0
endmodule

module gpr_rmux (
  input  en_r0,
  input  [7:0] d_r0,
  input  ck_r0,
  input  clr_r0,
  input  rmux1_sel_ab,
  input  rmux1_sel_top,
  input  en_r1,
  input  [7:0] d_r1,
  input  ck_r1,
  input  clr_r1,
  input  rmux1_sel_cd,
  input  en_r2,
  input  rmux2_sel_ab,
  input  [7:0] d_r2,
  input  ck_r2,
  input  clr_r2,
  input  rmux2_sel_top,
  input  rmux2_sel_cd,
  input  en_r3,
  input  [7:0] d_r3,
  input  ck_r3,
  input  clr_r3,
  output [1:0] raddr_out,
  output [7:0] rmux1_out,
  output [7:0] rmux2_out
);

  wire [1:0] multiplexer_1_out, multiplexer_2_out;
  wire [7:0] multiplexer_3_out, multiplexer_4_out, multiplexer_5_out, multiplexer_6_out, R0_q, R1_q, R2_q,
       R3_q;

  Register #(.width(8)) R0 (.D(d_r0), .Q(R0_q));  // open: en, clk, clr
  Register #(.width(8)) R1 (.D(d_r1), .Q(R1_q));  // open: en, clk, clr
  Register #(.width(8)) R2 (.D(d_r2), .Q(R2_q));  // open: en, clk, clr
  Register #(.width(8)) R3 (.D(d_r3), .Q(R3_q));  // open: en, clk, clr
  Multiplexer #(.width(2)) multiplexer_1 (.in0(2'b00), .in1(2'b00), .out(multiplexer_1_out), .sel(1'b0));  // open: en
  Multiplexer #(.width(2)) multiplexer_2 (
    .in0(multiplexer_1_out), .out(multiplexer_2_out), .sel(1'b0));  // open: in1, en
  Multiplexer #(.width(8)) multiplexer_3 (
    .in0(R0_q), .in1(R1_q), .out(multiplexer_3_out), .sel(rmux1_sel_ab));  // open: en
  Multiplexer #(.width(8)) multiplexer_4 (
    .in0(R2_q), .in1(R3_q), .out(multiplexer_4_out), .sel(rmux1_sel_cd));  // open: en
  Multiplexer #(.width(8)) multiplexer_5 (
    .in0(R0_q), .in1(R1_q), .out(multiplexer_5_out), .sel(rmux2_sel_ab));  // open: en
  Multiplexer #(.width(8)) multiplexer_6 (
    .in0(R2_q), .in1(R3_q), .out(multiplexer_6_out), .sel(rmux2_sel_cd));  // open: en
  Multiplexer #(.width(2)) multiplexer_7 (.in0(multiplexer_2_out), .out(raddr_out), .sel(1'b0));  // open: in1, en
  Multiplexer #(.width(8)) multiplexer_8 (
    .in0(multiplexer_3_out), .in1(multiplexer_4_out), .out(rmux1_out), .sel(rmux1_sel_top));  // open: en
  Multiplexer #(.width(8)) multiplexer_9 (
    .in0(multiplexer_5_out), .in1(multiplexer_6_out), .out(rmux2_out), .sel(rmux2_sel_top));  // open: en
endmodule

module alu (
  input  [7:0] a,
  input  [7:0] b,
  output [7:0] sum,
  output eq
);

  Adder #(.width(8)) adder_1 (.a(a), .b(b), .out(sum), .cin(1'b0));  // open: cout
  Comparator #(.width(8)) comparator_1 (.a(a), .b(b), .eq(eq));  // open: gt, lt
endmodule

module control (
  input  comp_eq,
  input  dec3,
  input  dec0,
  input  dec1,
  input  [1:0] waddr,
  output wen0,
  output branch_taken,
  output wen1,
  output is_gpr_write,
  output wen2,
  output wen3
);

  wire decoder_1_out0, decoder_1_out1, decoder_1_out2, decoder_1_out3, not_1_out, or_1_out;

  not not_1 (not_1_out, comp_eq);
  and and_1 (branch_taken, not_1_out, dec3);
  or or_1 (or_1_out, dec0, dec1);
  Decoder #(.select(2), .enable("false")) decoder_1 (
    .out0(decoder_1_out0), .out1(decoder_1_out1), .out2(decoder_1_out2), .out3(decoder_1_out3), .sel(waddr));
  buf or_2 (is_gpr_write, or_1_out);  // OR_Gate
  and and_2 (wen0, is_gpr_write, decoder_1_out0);
  and and_3 (wen1, is_gpr_write, decoder_1_out1);
  and and_4 (wen2, is_gpr_write, decoder_1_out2);
  and and_5 (wen3, is_gpr_write, decoder_1_out3);
endmodule

module writeback (
  input  [7:0] alu_result,
  input  is_li,
  input  is_io,
  input  [1:0] imm_in,
  input  [7:0] out_d,
  input  ck,
  input  clr,
  output [7:0] wdata,
  output [7:0] imm_out_to_mux
);

  wire [7:0] multiplexer_1_out;

  assign imm_out_to_mux = {{6{1'b0}}, imm_in};  // Bit_Extender bit_extender_1
  Shifter #(.width(8)) shifter_1 ();  // open: in, dist, out
  Multiplexer #(.width(8)) multiplexer_1 (
    .in0(alu_result), .in1(imm_out_to_mux), .out(multiplexer_1_out), .sel(is_li));  // open: en
  Register #(.width(8)) OUT (.D(out_d), .clk(ck), .clr(clr));  // open: en, Q
  Multiplexer #(.width(8)) multiplexer_2 (
    .in0(multiplexer_1_out), .in1({8{1'b0}}), .out(wdata), .sel(is_io));  // open: en
endmodule
