// Logisim project sCPU_F6.circ as structural Verilog: 1 circuit, main circuit main
module main (
  input  clk,
  input  rst
);

  wire and_1_out, and_3_out, and_4_out, and_5_out, and_6_out, comparator_1_eq, decoder_1_out0,
       decoder_1_out1, decoder_1_out2, decoder_1_out3, decoder_2_out0, decoder_2_out1, decoder_2_out2,
       decoder_2_out3, multiplexer_1_p3, not_1_out, or_1_out, or_2_out, undriven, undriven_2, undriven_3,
       undriven_4, undriven_5;
  wire [1:0] multiplexer_2_out, multiplexer_3_out, rom_1_p2, rom_1_p2_2, rom_1_p2_3, rom_1_p2_4;
  wire [7:0] adder_1_out, adder_2_out, bit_extender_1_out, bit_extender_2_out, multiplexer_4_out,
       multiplexer_5_p4, multiplexer_6_out, multiplexer_7_p4, multiplexer_9_out, multiplexer_10_out,
       multiplexer_11_out, multiplexer_12_out, PC_q, R0_q, R1_q, R2_q, R3_q;

  Register #(.width(8)) PC (.D(adder_1_out), .en(and_1_out), .Q(PC_q), .clk(clk), .clr(undriven));
  Adder #(.width(8)) adder_1 (.a(PC_q), .b(8'h1), .out(adder_1_out), .cin(1'b0));  // open: cout
  assign bit_extender_1_out = {{6{rom_1_p2[1]}}, rom_1_p2};  // Bit_Extender bit_extender_1
  // ROM #(.addrWidth(8), .dataWidth(8)) rom_1: pin names not known; wires that end beside it: PC_q, {rom_1_p2_4, rom_1_p2_3, rom_1_p2_2, rom_1_p2}
  // Multiplexer #(.width(8)) multiplexer_1: pin names not known; wires that end beside it: 8'h1, bit_extender_1_out, multiplexer_1_p3, adder_1_out
  and and_1 (and_1_out, rst, 1'b1);
  assign bit_extender_2_out = {{6{1'b0}}, rom_1_p2};  // Bit_Extender bit_extender_2
  Decoder #(.select(2), .enable("false")) decoder_1 (
    .out0(decoder_1_out0), .out1(decoder_1_out1), .out2(decoder_1_out2), .out3(decoder_1_out3),
    .sel(rom_1_p2_4));
  not not_1 (not_1_out, comparator_1_eq);
  Register #(.width(8)) R0 (.D(multiplexer_12_out), .en(and_3_out), .Q(R0_q), .clk(undriven_2), .clr(undriven_5));
  Register #(.width(8)) R1 (.D(multiplexer_12_out), .en(and_4_out), .Q(R1_q), .clk(undriven_3), .clr(undriven_5));
  Register #(.width(8)) R2 (.D(multiplexer_12_out), .en(and_5_out), .Q(R2_q), .clk(undriven_4), .clr(undriven_5));
  Register #(.width(8)) R3 (.D(multiplexer_12_out), .en(and_6_out), .Q(R3_q), .clk(clk), .clr(undriven_5));
  Shifter #(.width(8)) shifter_1 ();  // open: in, dist, out
  Multiplexer #(.width(2)) multiplexer_2 (.in0(2'b00), .in1(2'b00), .out(multiplexer_2_out), .sel(1'b0));  // open: en
  and and_2 (multiplexer_1_p3, not_1_out, decoder_1_out3);
  or or_1 (or_1_out, decoder_1_out0, decoder_1_out1);
  Decoder #(.select(2), .enable("false")) decoder_2 (
    .out0(decoder_2_out0), .out1(decoder_2_out1), .out2(decoder_2_out2), .out3(decoder_2_out3),
    .sel(rom_1_p2_3));
  Multiplexer #(.width(2)) multiplexer_3 (
    .in0(multiplexer_2_out), .out(multiplexer_3_out), .sel(1'b0));  // open: in1, en
  Multiplexer #(.width(8)) multiplexer_4 (
    .in0(R0_q), .in1(R1_q), .out(multiplexer_4_out), .sel(rom_1_p2_2[0]));  // open: en
  // Multiplexer #(.width(8)) multiplexer_5: pin names not known; wires that end beside it: R2_q, R3_q, rom_1_p2_2[0], multiplexer_5_p4
  Multiplexer #(.width(8)) multiplexer_6 (
    .in0(R0_q), .in1(R1_q), .out(multiplexer_6_out), .sel(rom_1_p2[0]));  // open: en
  // Multiplexer #(.width(8)) multiplexer_7: pin names not known; wires that end beside it: R2_q, R3_q, rom_1_p2[0], multiplexer_7_p4
  Multiplexer #(.width(2)) multiplexer_8 (.in0(multiplexer_3_out), .out(rom_1_p2_3), .sel(1'b0));  // open: in1, en
  buf or_2 (or_2_out, or_1_out);  // OR_Gate
  Multiplexer #(.width(8)) multiplexer_9 (
    .in0(multiplexer_4_out), .in1(multiplexer_5_p4), .out(multiplexer_9_out), .sel(rom_1_p2_2[1]));  // open: en
  Multiplexer #(.width(8)) multiplexer_10 (
    .in0(multiplexer_6_out), .in1(multiplexer_7_p4), .out(multiplexer_10_out), .sel(rom_1_p2[1]));  // open: en
  and and_3 (and_3_out, or_2_out, decoder_2_out0);
  and and_4 (and_4_out, or_2_out, decoder_2_out1);
  and and_5 (and_5_out, or_2_out, decoder_2_out2);
  and and_6 (and_6_out, or_2_out, decoder_2_out3);
  Adder #(.width(8)) adder_2 (
    .a(multiplexer_9_out), .b(multiplexer_10_out), .out(adder_2_out), .cin(1'b0));  // open: cout
  Comparator #(.width(8)) comparator_1 (
    .a(multiplexer_9_out), .b(multiplexer_10_out), .eq(comparator_1_eq));  // open: gt, lt
  Multiplexer #(.width(8)) multiplexer_11 (
    .in0(adder_2_out), .in1(bit_extender_2_out), .out(multiplexer_11_out), .sel(decoder_1_out0));  // open: en
  Register #(.width(8)) OUT (.D(multiplexer_9_out), .en(decoder_1_out2), .clk(clk), .clr(rst));  // open: Q
  Multiplexer #(.width(8)) multiplexer_12 (
    .in0(multiplexer_11_out), .in1({8{1'b0}}), .out(multiplexer_12_out), .sel(decoder_1_out2));  // open: en

  // Notes on the sheet:
  //   contents of rom_1 (hex, n*v repeats v):
  //   0 90     1 a1     2 be     3 16     4 29     5 f7     6 54     7 0
endmodule
